// Logisim project InstructionReg.circ as structural Verilog: 1 circuit, main circuit main
module main (
  input  in_1,
  input  in_2,
  input  [31:0] in_3,
  output out_4,
  output Branc,
  output WE,
  output WREN,
  output Jump,
  output JRA,
  output [1:0] out_10,
  output out_11,
  output RD3SourceSelect,
  output [15:0] out_13,
  output [1:0] out_14,
  output [5:0] out_15,
  output out_16,
  output out_17,
  output out_18,
  output out_19,
  output out_20,
  output out_21,
  output out_22,
  output out_23,
  output out_24,
  output out_25,
  output out_26,
  output out_27,
  output JMP,
  output JRA_2,
  output Branch,
  output MemWe,
  output RD3Source,
  output AluInputMux,
  output out_34,
  output ALUOP,
  output MTRDATR,
  output out_37,
  output Memload,
  output RegFileWE
);

  wire and_3_out, and_5_out, and_7_out, and_8_out, and_9_out, and_10_out, and_11_out, and_12_out, and_13_out,
       and_14_out, and_15_out, and_16_out, and_18_out, and_20_out, and_21_out, and_22_out, and_23_out,
       and_24_out, and_25_out, bitfinder_1_found, bitselector_16_out, bitselector_24_out, clock_1_out,
       clock_2_out, clock_3_out, decoder_1_out0, decoder_1_out1, decoder_1_out2, decoder_1_out3,
       decoder_1_out4, decoder_1_out5, decoder_1_out6, decoder_1_out7, decoder_1_out8, decoder_1_out9,
       not_1_out, not_2_out, not_3_out, not_4_out, not_5_out, not_6_out, not_7_out, not_8_out, not_9_out,
       not_10_out, not_11_out, not_12_out, not_13_out, not_14_out, not_15_out, not_16_out, not_17_out,
       not_18_out, not_19_out, undriven;
  wire [4:0] bitselector_8_out, bitselector_12_out, bitselector_13_out, multiplexer_4_out, register_3_q;
  wire [5:0] bitselector_7_out;
  wire [10:0] bitselector_10_out;
  wire [15:0] bitselector_9_out;
  wire [20:0] bitselector_5_out;
  wire [23:0] bit_extender_1_out, bit_extender_5_out, register_1_q;
  wire [25:0] bitselector_2_out, bitselector_4_out;
  wire [31:0] adder_1_out, adder_2_out, adder_3_out, and_26_out, bit_extender_2_out, bit_extender_3_out,
       bit_extender_4_out, bit_extender_6_out, bit_extender_7_out, multiplexer_1_out, multiplexer_2_out,
       multiplexer_3_out, multiplexer_5_out, multiplexer_6_out, multiplexer_7_out, multiplexer_8_out,
       multiplexer_9_out, or_1_out, ram_1_data, register_5_q, register_6_q, register_7_q, register_8_q,
       register_9_q, register_10_q, register_11_q, register_12_q, register_13_q, register_14_q, rom_1_data,
       shifter_1_out, shifter_2_out, shifter_3_out, subtractor_1_out;

  Multiplexer #(.width(32), .enable("false")) multiplexer_1 (
    .in0(adder_1_out), .in1(adder_2_out), .out(multiplexer_1_out), .sel(and_25_out));
  Multiplexer #(.width(32), .enable("false")) multiplexer_2 (
    .in0(multiplexer_1_out), .in1(multiplexer_6_out), .out(multiplexer_2_out), .sel(JRA));
  Adder #(.width(32)) adder_1 (.a(32'h1), .b(bit_extender_2_out), .out(adder_1_out));  // open: cin, cout
  Shifter #(.width(32)) shifter_1 (.in(bit_extender_4_out), .\dist ({5{1'b0}}), .out(shifter_1_out));
  Bit_Extender #(.in_width(32), .out_width(24)) bit_extender_1 (.in(multiplexer_3_out), .out(bit_extender_1_out));
  Clock clock_1 (.out(clock_1_out));
  Adder #(.width(32)) adder_2 (.a(adder_1_out), .b(shifter_1_out), .out(adder_2_out));  // open: cin, cout
  Multiplexer #(.width(32), .enable("false")) multiplexer_3 (
    .in0(multiplexer_2_out), .in1(shifter_2_out), .out(multiplexer_3_out), .sel(JMP));
  Register #(.width(24)) register_1 (
    .D(bit_extender_1_out), .en(1'b1), .Q(register_1_q), .clk(clock_1_out), .clr(in_2));
  assign bit_extender_2_out = {{8{1'b0}}, register_1_q};  // Bit_Extender bit_extender_2
  Clock clock_2 (.out(clock_2_out));
  not not_1 (not_1_out, out_17);
  not not_2 (not_2_out, out_18);
  not not_3 (not_3_out, out_19);
  and and_1 (Memload, out_16, not_1_out, not_2_out, not_3_out, bitselector_16_out, out_21);
  Shifter #(.width(32)) shifter_2 (.in(bit_extender_3_out), .\dist ({5{1'b0}}), .out(shifter_2_out));
  ROM #(.addrWidth(24), .dataWidth(32)) rom_1 (.addr(register_1_q), .data(rom_1_data), .sel(1'b1));
  Register #(.width(6)) register_2 (.D(bitselector_7_out), .en(1'b1), .clk(clock_2_out));  // open: Q, clr
  BitSelector #(.width(32), .group(16)) bitselector_1 (.in(rom_1_data), .out(out_13), .sel(1'b0));
  BitSelector #(.width(32), .group(26)) bitselector_2 (.in(rom_1_data), .out(bitselector_2_out), .sel(1'b0));
  assign bit_extender_3_out = {{6{1'b0}}, bitselector_2_out};  // Bit_Extender bit_extender_3
  BitSelector #(.width(6)) bitselector_3 (.in(bitselector_7_out), .out(out_16), .sel(3'b101));
  not not_4 (not_4_out, out_17);
  not not_5 (not_5_out, out_19);
  and and_2 (MemWe, out_16, not_4_out, out_18, not_5_out, bitselector_16_out, out_21);
  BitSelector #(.width(32), .group(26)) bitselector_4 (.in(rom_1_data), .out(bitselector_4_out), .sel(1'b1));
  BitSelector #(.width(32), .group(21)) bitselector_5 (.in(rom_1_data), .out(bitselector_5_out), .sel(1'b1));
  BitSelector #(.width(6)) bitselector_6 (.in(bitselector_7_out), .out(out_17), .sel(3'b100));
  not not_6 (not_6_out, out_17);
  not not_7 (not_7_out, out_16);
  and and_3 (and_3_out, not_7_out, not_6_out, out_18, not_9_out, not_8_out, not_10_out);
  BitSelector #(.width(26), .group(6)) bitselector_7 (.in(bitselector_4_out), .out(bitselector_7_out), .sel(3'b000));
  BitSelector #(.width(21), .group(5)) bitselector_8 (.in(bitselector_5_out), .out(bitselector_8_out), .sel(3'b000));
  Register #(.width(5)) register_3 (
    .D(bitselector_8_out), .en(1'b1), .Q(register_3_q), .clk(clock_2_out));  // open: clr
  BitSelector #(.width(32), .group(16)) bitselector_9 (.in(rom_1_data), .out(bitselector_9_out), .sel(1'b1));
  BitSelector #(.width(32), .group(11)) bitselector_10 (.in(rom_1_data), .out(bitselector_10_out), .sel(2'b01));
  BitSelector #(.width(6)) bitselector_11 (.in(bitselector_7_out), .out(out_18), .sel(3'b011));
  not not_8 (not_8_out, bitselector_16_out);
  not not_9 (not_9_out, out_19);
  not not_10 (not_10_out, out_21);
  BitSelector #(.width(16), .group(5)) bitselector_12 (.in(bitselector_9_out), .out(bitselector_12_out), .sel(2'b00));
  BitSelector #(.width(11), .group(5)) bitselector_13 (.in(bitselector_10_out), .out(bitselector_13_out), .sel(2'b00));
  assign bit_extender_4_out = {{16{out_13[15]}}, out_13};  // Bit_Extender bit_extender_4
  BitSelector #(.width(32), .group(6)) bitselector_14 (.in(rom_1_data), .out(out_15), .sel(3'b000));
  BitSelector #(.width(6)) bitselector_15 (.in(bitselector_7_out), .out(out_19), .sel(3'b010));
  not not_11 (not_11_out, out_18);
  and and_4 (Branc, not_7_out, not_6_out, not_11_out, out_19, not_8_out, not_10_out);
  Decoder #(.select(5)) decoder_1 (
    .out0(decoder_1_out0), .out1(decoder_1_out1), .out2(decoder_1_out2), .out3(decoder_1_out3),
    .out4(decoder_1_out4), .out5(decoder_1_out5), .out6(decoder_1_out6), .out7(decoder_1_out7),
    .out8(decoder_1_out8), .out9(decoder_1_out9), .sel(multiplexer_4_out), .en(1'b1));  // open: out10, out11, out12, out13, out14, out15, out16, out17, out18, out19, out20, out21, out22, out23, out24, out25, out26, out27, out28, out29, out30, out31
  Register #(.width(5)) register_4 (.D(bitselector_12_out), .en(1'b1), .clk(clock_2_out));  // open: Q, clr
  Multiplexer #(.width(5), .enable("false")) multiplexer_4 (
    .in0(bitselector_12_out), .in1(bitselector_13_out), .out(multiplexer_4_out), .sel(RD3Source));
  and and_5 (and_5_out, not_7_out, not_6_out, out_18, out_19, bitselector_16_out, out_21);
  BitSelector #(.width(6)) bitselector_16 (.in(bitselector_7_out), .out(bitselector_16_out), .sel(3'b001));
  BitSelector #(.width(6)) bitselector_17 (.in(bitselector_7_out), .out(out_21), .sel(3'b000));
  and and_6 (JMP, not_7_out, not_6_out, not_2_out, not_9_out, bitselector_16_out, not_10_out);
  and and_7 (and_7_out, RegFileWE, decoder_1_out0);
  and and_8 (and_8_out, RegFileWE, decoder_1_out1);
  and and_9 (and_9_out, RegFileWE, decoder_1_out2);
  and and_10 (and_10_out, RegFileWE, decoder_1_out3);
  and and_11 (and_11_out, RegFileWE, decoder_1_out4);
  and and_12 (and_12_out, RegFileWE, decoder_1_out5);
  and and_13 (and_13_out, RegFileWE, decoder_1_out6);
  and and_14 (and_14_out, RegFileWE, decoder_1_out7);
  and and_15 (and_15_out, RegFileWE, decoder_1_out8);
  and and_16 (and_16_out, RegFileWE, decoder_1_out9);
  Register #(.width(32)) register_5 (.en(and_7_out), .Q(register_5_q), .clk(clock_3_out), .clr(undriven));  // open: D
  Register #(.width(32)) register_6 (
    .D(multiplexer_9_out), .en(and_8_out), .Q(register_6_q), .clk(clock_3_out), .clr(undriven));
  Register #(.width(32)) register_7 (
    .D(multiplexer_9_out), .en(and_9_out), .Q(register_7_q), .clk(clock_3_out), .clr(undriven));
  Register #(.width(32)) register_8 (
    .D(multiplexer_9_out), .en(and_10_out), .Q(register_8_q), .clk(clock_3_out), .clr(undriven));
  Register #(.width(32)) register_9 (
    .D(multiplexer_9_out), .en(and_11_out), .Q(register_9_q), .clk(clock_3_out), .clr(undriven));
  Register #(.width(32)) register_10 (
    .D(multiplexer_9_out), .en(and_12_out), .Q(register_10_q), .clk(clock_3_out), .clr(undriven));
  Register #(.width(32)) register_11 (
    .D(multiplexer_9_out), .en(and_13_out), .Q(register_11_q), .clk(clock_3_out), .clr(undriven));
  Register #(.width(32)) register_12 (
    .D(multiplexer_9_out), .en(and_14_out), .Q(register_12_q), .clk(clock_3_out), .clr(undriven));
  Register #(.width(32)) register_13 (
    .D(multiplexer_9_out), .en(and_15_out), .Q(register_13_q), .clk(clock_3_out), .clr(undriven));
  Register #(.width(32)) register_14 (
    .D(multiplexer_9_out), .en(and_16_out), .Q(register_14_q), .clk(clock_3_out), .clr(undriven));
  BitSelector #(.width(6)) bitselector_18 (.in(out_15), .out(out_22), .sel(3'b101));
  and and_17 (RD3Source, not_7_out, not_6_out, not_2_out, not_9_out, not_8_out, not_10_out);
  BitSelector #(.width(6)) bitselector_19 (.in(out_15), .out(out_23), .sel(3'b100));
  not not_12 (not_12_out, out_22);
  and and_18 (and_18_out, RD3Source, not_17_out);
  BitSelector #(.width(6)) bitselector_20 (.in(out_15), .out(out_24), .sel(3'b011));
  not not_13 (not_13_out, out_23);
  not not_14 (not_14_out, out_25);
  not not_15 (not_15_out, out_27);
  not not_16 (not_16_out, out_26);
  and and_19 (JRA, RD3Source, not_12_out, not_13_out, out_24, not_14_out, not_16_out, not_15_out);
  not not_17 (not_17_out, JRA);
  BitSelector #(.width(6)) bitselector_21 (.in(out_15), .out(out_25), .sel(3'b010));
  not not_18 (not_18_out, out_24);
  and and_20 (and_20_out, RD3Source, not_18_out, not_14_out, not_16_out, not_15_out);
  Multiplexer #(.select(5), .width(32)) multiplexer_5 (
    .in0(register_5_q), .in1(register_6_q), .in2(register_7_q), .in3(register_8_q), .in4(register_9_q),
    .in5(register_10_q), .in6(register_11_q), .in7(register_12_q), .in8(register_13_q), .in9(register_14_q),
    .out(multiplexer_5_out), .sel(bitselector_8_out), .en(1'b1));  // open: in10, in11, in12, in13, in14, in15, in16, in17, in18, in19, in20, in21, in22, in23, in24, in25, in26, in27, in28, in29, in30, in31
  Multiplexer #(.select(5), .width(32)) multiplexer_6 (
    .in0(register_5_q), .in1(register_6_q), .in2(register_7_q), .in3(register_8_q), .in4(register_9_q),
    .in5(register_10_q), .in6(register_11_q), .in7(register_12_q), .in8(register_13_q), .in9(register_14_q),
    .out(multiplexer_6_out), .sel(bitselector_12_out), .en(1'b1));  // open: in10, in11, in12, in13, in14, in15, in16, in17, in18, in19, in20, in21, in22, in23, in24, in25, in26, in27, in28, in29, in30, in31
  BitSelector #(.width(6)) bitselector_22 (.in(out_15), .out(out_26), .sel(3'b001));
  and and_21 (and_21_out, RD3Source, not_18_out, not_14_out, out_26, not_15_out);
  BitSelector #(.width(6)) bitselector_23 (.in(out_15), .out(out_27), .sel(3'b000));
  and and_22 (and_22_out, RD3Source, not_18_out, out_25, not_16_out, not_15_out);
  Clock clock_3 (.out(clock_3_out));
  and and_23 (and_23_out, RD3Source, not_18_out, out_25, not_16_out, out_27);
  Multiplexer #(.width(32), .enable("false")) multiplexer_7 (
    .in0(multiplexer_6_out), .in1(bit_extender_4_out), .out(multiplexer_7_out), .sel(AluInputMux));
  and and_24 (and_24_out, RD3Source, out_24, not_14_out, out_26, not_15_out);
  Adder #(.width(32)) adder_3 (
    .a(multiplexer_5_out), .b(multiplexer_7_out), .out(adder_3_out), .cin(1'b0));  // open: cout
  Subtractor #(.width(32)) subtractor_1 (
    .a(multiplexer_5_out), .b(multiplexer_7_out), .out(subtractor_1_out), .bin(1'b0));  // open: bout
  assign or_1_out = multiplexer_5_out | multiplexer_7_out;  // OR_Gate or_1, 32 bits wide
  BitFinder #(.width(32)) bitfinder_1 (.in(multiplexer_8_out), .found(bitfinder_1_found));  // open: index
  not not_19 (not_19_out, bitfinder_1_found);
  and and_25 (and_25_out, Branc, not_19_out);
  assign and_26_out = multiplexer_5_out & multiplexer_7_out;  // AND_Gate and_26, 32 bits wide
  Multiplexer #(.select(2), .width(32)) multiplexer_8 (
    .in0(and_26_out), .in1(adder_3_out), .in2(subtractor_1_out), .in3(or_1_out), .out(multiplexer_8_out),
    .sel({out_10[1], ALUOP}), .en(1'b1));
  or or_2 (out_10[1], and_21_out, and_23_out, and_24_out, Branc);
  Shifter #(.width(32)) shifter_3 (.in(bit_extender_4_out), .\dist (5'b10000), .out(shifter_3_out));
  or or_3 (AluInputMux, Memload, MemWe, and_3_out);
  or or_4 (RegFileWE, Memload, and_3_out, and_18_out, and_5_out);
  or or_5 (ALUOP, Memload, MemWe, and_3_out, and_20_out, and_23_out);
  or or_6 (MTRDATR, and_5_out, and_24_out);
  or or_7 (out_14[0], and_3_out, RD3Source);
  Bit_Extender #(.in_width(32), .out_width(24)) bit_extender_5 (.in(multiplexer_8_out), .out(bit_extender_5_out));
  BitSelector #(.width(32)) bitselector_24 (.in(multiplexer_8_out), .out(bitselector_24_out), .sel({5{1'b1}}));
  assign bit_extender_6_out = {{31{1'b0}}, bitselector_24_out};  // Bit_Extender bit_extender_6
  assign bit_extender_7_out = {{8{1'b0}}, bit_extender_5_out};  // Bit_Extender bit_extender_7
  Multiplexer #(.select(2), .width(32), .enable("false")) multiplexer_9 (
    .in0(ram_1_data), .in1(bit_extender_7_out), .in2(shifter_3_out), .in3(bit_extender_6_out),
    .out(multiplexer_9_out), .sel({MTRDATR, out_14[0]}));
  RAM #(.addrWidth(24), .dataWidth(32), .bus("separate")) ram_1 (
    .addr(bit_extender_5_out), .din(multiplexer_6_out), .data(ram_1_data), .str(MemWe), .sel(1'b1),
    .clk(clock_3_out), .ld(Memload), .clr(in_1));

  assign Branch = Branc;
  assign JRA_2 = JRA;
  assign Jump = JMP;
  assign out_4 = Memload;
  assign out_10[0] = ALUOP;
  assign out_11 = AluInputMux;
  assign out_14[1] = MTRDATR;
  assign out_20 = out_19;
  assign out_34 = out_10[1];
  assign out_37 = out_14[0];
  assign RD3SourceSelect = RD3Source;
  assign WE = MemWe;
  assign WREN = RegFileWE;

  // Notes on the sheet:
  //   in_2: pull=down
  //   Data Memoriye 24 bit adresleme mecburi rom en yüksek 24 bit adresleme yapıyor...
  //   lw
  //   contents of rom_1 (hex, n*v repeats v):
  //   2002000a 20010000 20040000 22182a 10030004 812020 20210001 ac240000 8000003 8000009
  //   sw
  //   31:26
  //   25:21
  //   15:0
  //   20:16
  //   opcode
  //   addi
  //   beg
  //   RD1
  //   RD2
  //   fnc
  //   Controller
  //   lui
  //   jump
  //   jump
  //   R-type
  //   DATA
  //   jr
  //   add
  //   sub
  //   and
  //   or
  //   Alu Select
  //   slt
  //   ALUSELECT
  //   Memload
  //   slt a<b ilk bit 1 olacak
  //   MemClear
  //   MemtoREg
  //   or ALU to reg
endmodule
