// Logisim project MyProcessor.circ as structural Verilog: 1 circuit, main circuit main
module main (
  input  in_1,
  input  in_2,
  input  in_3,
  input  in_4,
  input  in_5,
  input  in_6,
  input  in_7,
  input  in_8,
  input  in_9,
  input  in_10,
  input  [6:0] in_11,
  input  in_12,
  input  in_13,
  input  in_14,
  output SpecialRegEnable,
  output Bra,
  output [4:0] out_17,
  output [3:0] out_18,
  output WRE,
  output [3:0] out_20,
  output out_21,
  output BRE_BRNE,
  output [4:0] out_23,
  output [2:0] out_24,
  output ALU_SRC,
  output JRA,
  output LoadOutput,
  output out_28,
  output WRE_2,
  output out_30,
  output jmp,
  output [4:0] RD2,
  output [2:0] out_33,
  output out_34,
  output out_35,
  output out_36,
  output out_37,
  output out_38,
  output out_39,
  output out_40,
  output out_41,
  output out_42,
  output BRAEN,
  output BRE_NE,
  output JRA_2,
  output out_46,
  output out_47,
  output ALUSRC,
  output WRE_3,
  output LD,
  output out_51,
  output out_52,
  output MTRRTM,
  output out_54,
  output J,
  output out_56,
  output out_57,
  output out_58,
  output BRA_2,
  output out_60,
  output savepc
);

  wire addi_out, and_1_out, and_2_out, and_3_out, and_4_out, and_5_out, and_7_out, and_8_out, and_9_out,
       and_10_out, and_11_out, and_12_out, and_13_out, and_14_out, and_15_out, and_16_out, and_17_out,
       and_18_out, and_19_out, and_20_out, and_21_out, and_23_out, and_24_out, and_25_out, and_26_out,
       and_27_out, and_28_out, and_29_out, and_31_out, and_33_out, and_34_out, and_35_out, and_37_out,
       and_38_out, and_39_out, and_40_out, and_41_out, bitfinder_1_found, bitselector_22_out, clock_1_out,
       clock_2_out, clock_3_out, clock_4_out, decoder_1_out0, decoder_1_out1, decoder_1_out2, decoder_1_out3,
       decoder_1_out4, decoder_1_out5, decoder_1_out6, decoder_1_out7, decoder_1_out8, decoder_1_out9,
       decoder_1_out10, decoder_1_out11, decoder_1_out12, decoder_1_out13, decoder_1_out14, decoder_2_out0,
       decoder_2_out1, decoder_2_out2, decoder_2_out3, decoder_2_out4, decoder_2_out5, decoder_2_out6,
       decoder_2_out7, IN_out, lui_out, multiplexer_10_out, not_1_out, not_2_out, not_3_out, not_4_out,
       not_5_out, not_6_out, not_7_out, not_8_out, not_9_out, not_10_out, not_11_out, shr_out, swi_out;
  wire [3:0] bit_extender_9_out, bitselector_17_out;
  wire [4:0] bit_extender_4_out, bitselector_12_out, multiplexer_4_out;
  wire [7:0] bit_extender_10_out, buffer_1_out, multiplexer_13_out, register_17_q, register_18_q,
       register_19_q, register_20_q, register_21_q, register_22_q, register_23_q, register_24_q;
  wire [16:0] bitselector_7_out;
  wire [21:0] bitselector_5_out, bitselector_6_out;
  wire [23:0] bit_extender_1_out, bit_extender_5_out, bit_extender_6_out, multiplexer_11_out;
  wire [26:0] bitselector_1_out, bitselector_2_out, bitselector_4_out;
  wire [31:0] adder_1_out, adder_2_out, and_32_out, bit_extender_2_out, bit_extender_3_out,
       bit_extender_7_out, bit_extender_8_out, divider_1_out, multiplexer_1_out, multiplexer_2_out,
       multiplexer_3_out, multiplexer_5_out, multiplexer_6_out, multiplexer_7_out, multiplexer_8_out,
       multiplexer_9_out, multiplexer_12_out, multiplier_1_out, or_2_out, ram_1_data, register_1_q,
       register_2_q, register_3_q, register_4_q, register_5_q, register_6_q, register_7_q, register_8_q,
       register_9_q, register_10_q, register_11_q, register_12_q, register_13_q, register_14_q,
       register_15_q, register_16_q, rom_1_data, shifter_1_out, shifter_2_out, subtractor_1_out, undriven;

  Clock clock_1 (.out(clock_1_out));
  and OUT (out_60, not_5_out, not_1_out, out_36, out_37, not_4_out);
  and IN (IN_out, not_5_out, not_1_out, out_36, not_3_out, out_38);
  Register #(.width(32)) register_1 (
    .D(multiplexer_3_out), .en(1'b1), .Q(register_1_q), .clk(clock_1_out), .clr(in_10));
  Multiplexer #(.width(32), .enable("false")) multiplexer_1 (
    .in0(32'h1), .in1(32'h2), .out(multiplexer_1_out), .sel(and_33_out));
  Multiplexer #(.width(32), .enable("false")) multiplexer_2 (
    .in0(adder_1_out), .in1(multiplexer_5_out), .out(multiplexer_2_out), .sel(JRA));
  Multiplexer #(.width(32), .enable("false")) multiplexer_3 (
    .in0(multiplexer_2_out), .in1(bit_extender_2_out), .out(multiplexer_3_out), .sel(J));
  and u_SavePC (savepc, not_5_out, out_35, not_2_out, not_3_out, out_38);
  Adder #(.width(32)) adder_1 (.a(register_1_q), .b(multiplexer_1_out), .out(adder_1_out), .cin(1'b0));  // open: cout
  and and_1 (and_1_out, not_5_out, not_1_out, not_2_out, out_37, not_4_out);
  Bit_Extender #(.in_width(32), .out_width(24)) bit_extender_1 (.in(register_1_q), .out(bit_extender_1_out));
  assign bit_extender_2_out = {{5{1'b0}}, bitselector_1_out};  // Bit_Extender bit_extender_2
  BitSelector #(.width(32), .group(27)) bitselector_1 (.in(rom_1_data), .out(bitselector_1_out), .sel(1'b0));
  and addi (addi_out, not_5_out, not_1_out, not_2_out, out_37, out_38);
  and swi (swi_out, not_5_out, not_1_out, not_2_out, not_3_out, out_38);
  and lui (lui_out, not_5_out, not_1_out, out_36, out_37, out_38);
  ROM #(.addrWidth(24), .dataWidth(32)) rom_1 (.addr(bit_extender_1_out), .data(rom_1_data));  // open: sel
  BitSelector #(.width(32), .group(27)) bitselector_2 (.in(rom_1_data), .out(bitselector_2_out), .sel(1'b1));
  BitSelector #(.width(5)) bitselector_3 (.in(bitselector_12_out), .out(out_34), .sel(3'b100));
  not not_1 (not_1_out, out_35);
  not not_2 (not_2_out, out_36);
  not not_3 (not_3_out, out_37);
  and and_2 (and_2_out, out_34, not_1_out, not_2_out, not_3_out, not_4_out);
  BitSelector #(.width(32), .group(27)) bitselector_4 (.in(rom_1_data), .out(bitselector_4_out), .sel(1'b1));
  BitSelector #(.width(32), .group(22)) bitselector_5 (.in(rom_1_data), .out(bitselector_5_out), .sel(1'b1));
  BitSelector #(.width(32), .group(22)) bitselector_6 (.in(rom_1_data), .out(bitselector_6_out), .sel(1'b0));
  BitSelector #(.width(32), .group(17)) bitselector_7 (.in(rom_1_data), .out(bitselector_7_out), .sel(1'b1));
  BitSelector #(.width(5)) bitselector_8 (.in(bitselector_12_out), .out(out_35), .sel(3'b011));
  not not_4 (not_4_out, out_38);
  not not_5 (not_5_out, out_34);
  and and_3 (and_3_out, not_5_out, out_35, not_2_out, not_3_out, not_4_out);
  BitSelector #(.width(27), .group(5)) bitselector_9 (.in(bitselector_4_out), .out(out_17), .sel(3'b000));
  BitSelector #(.width(22), .group(5)) bitselector_10 (.in(bitselector_5_out), .out(out_23), .sel(3'b000));
  BitSelector #(.width(17), .group(5)) bitselector_11 (.in(bitselector_7_out), .out(RD2), .sel(2'b00));
  BitSelector #(.width(27), .group(5)) bitselector_12 (.in(bitselector_2_out), .out(bitselector_12_out), .sel(3'b000));
  BitSelector #(.width(5)) bitselector_13 (.in(bitselector_12_out), .out(out_36), .sel(3'b010));
  BitSelector #(.width(5)) bitselector_14 (.in(bitselector_12_out), .out(out_37), .sel(3'b001));
  and and_4 (and_4_out, out_34, out_35, not_2_out, not_3_out, not_4_out);
  Multiplexer #(.width(5), .enable("false")) multiplexer_4 (
    .in0(out_23), .in1(5'b01001), .out(multiplexer_4_out), .sel(out_30));
  Decoder #(.select(5), .enable("false")) decoder_1 (
    .out0(decoder_1_out0), .out1(decoder_1_out1), .out2(decoder_1_out2), .out3(decoder_1_out3),
    .out4(decoder_1_out4), .out5(decoder_1_out5), .out6(decoder_1_out6), .out7(decoder_1_out7),
    .out8(decoder_1_out8), .out9(decoder_1_out9), .out10(decoder_1_out10), .out11(decoder_1_out11),
    .out12(decoder_1_out12), .out13(decoder_1_out13), .out14(decoder_1_out14), .sel(multiplexer_4_out));  // open: out15, out16, out17, out18, out19, out20, out21, out22, out23, out24, out25, out26, out27, out28, out29, out30, out31
  assign bit_extender_3_out = {{10{bitselector_6_out[21]}}, bitselector_6_out};  // Bit_Extender bit_extender_3
  BitSelector #(.width(5)) bitselector_15 (.in(bitselector_12_out), .out(out_38), .sel(3'b000));
  and and_5 (and_5_out, out_34, not_1_out, out_36, not_3_out, not_4_out);
  Clock clock_2 (.out(clock_2_out));
  and and_6 (BRE_BRNE, out_34, out_35, out_36, not_3_out, not_4_out);
  and and_7 (and_7_out, decoder_1_out0, out_47);
  and and_8 (and_8_out, decoder_1_out1, out_47);
  and and_9 (and_9_out, decoder_1_out2, out_47);
  and and_10 (and_10_out, decoder_1_out3, out_47);
  and and_11 (and_11_out, decoder_1_out4, out_47);
  and and_12 (and_12_out, decoder_1_out5, out_47);
  and and_13 (and_13_out, decoder_1_out6, out_47);
  and and_14 (and_14_out, decoder_1_out7, out_47);
  and and_15 (and_15_out, decoder_1_out8, out_47);
  and and_16 (and_16_out, decoder_1_out9, out_47);
  and and_17 (and_17_out, decoder_1_out10, out_47);
  and and_18 (and_18_out, decoder_1_out11, out_47);
  and and_19 (and_19_out, decoder_1_out12, out_47);
  and and_20 (and_20_out, decoder_1_out13, out_47);
  and and_21 (and_21_out, decoder_1_out14, out_47);
  and and_22 (J, not_5_out, out_35, out_36, not_3_out, not_4_out);
  Register #(.width(32)) register_2 (
    .D(multiplexer_12_out), .en(and_7_out), .Q(register_2_q), .clk(clock_2_out), .clr(in_2));
  Register #(.width(32)) register_3 (
    .D(multiplexer_12_out), .en(and_8_out), .Q(register_3_q), .clk(clock_2_out), .clr(in_2));
  Register #(.width(32)) register_4 (
    .D(multiplexer_12_out), .en(and_9_out), .Q(register_4_q), .clk(clock_2_out), .clr(in_2));
  Register #(.width(32)) register_5 (
    .D(multiplexer_12_out), .en(and_10_out), .Q(register_5_q), .clk(clock_2_out), .clr(in_2));
  Register #(.width(32)) register_6 (
    .D(multiplexer_12_out), .en(and_11_out), .Q(register_6_q), .clk(clock_2_out), .clr(in_2));
  Register #(.width(32)) register_7 (
    .D(multiplexer_12_out), .en(and_12_out), .Q(register_7_q), .clk(clock_2_out), .clr(in_2));
  Register #(.width(32)) register_8 (
    .D(multiplexer_12_out), .en(and_13_out), .Q(register_8_q), .clk(clock_2_out), .clr(in_2));
  Register #(.width(32)) register_9 (
    .D(multiplexer_12_out), .en(and_14_out), .Q(register_9_q), .clk(clock_2_out), .clr(in_2));
  Register #(.width(32)) register_10 (
    .D(multiplexer_12_out), .en(and_15_out), .Q(register_10_q), .clk(clock_2_out), .clr(in_2));
  Register #(.width(32)) register_11 (
    .D(multiplexer_12_out), .en(and_16_out), .Q(register_11_q), .clk(clock_2_out), .clr(in_2));
  Register #(.width(32)) register_12 (
    .D(multiplexer_12_out), .en(and_17_out), .Q(register_12_q), .clk(clock_2_out), .clr(in_2));
  Register #(.width(32)) register_13 (
    .D(multiplexer_12_out), .en(and_18_out), .Q(register_13_q), .clk(clock_2_out), .clr(in_2));
  Register #(.width(32)) register_14 (
    .D(multiplexer_12_out), .en(and_19_out), .Q(register_14_q), .clk(clock_2_out), .clr(in_2));
  Register #(.width(32)) register_15 (
    .D(multiplexer_12_out), .en(and_20_out), .Q(register_15_q), .clk(clock_2_out), .clr(in_2));
  Register #(.width(32)) register_16 (
    .D(multiplexer_12_out), .en(and_21_out), .Q(register_16_q), .clk(clock_2_out), .clr(in_2));
  and and_23 (and_23_out, not_5_out, not_1_out, not_2_out, not_3_out, not_4_out);
  BitSelector #(.width(4)) bitselector_16 (.in(bitselector_17_out), .out(out_39), .sel(2'b11));
  and shr (shr_out, not_6_out, out_40, not_8_out, not_9_out, and_23_out);
  BitSelector #(.width(32), .group(4)) bitselector_17 (.in(rom_1_data), .out(bitselector_17_out), .sel(3'b000));
  BitSelector #(.width(4)) bitselector_18 (.in(bitselector_17_out), .out(out_40), .sel(2'b10));
  not not_6 (not_6_out, out_39);
  not not_7 (not_7_out, out_40);
  not not_8 (not_8_out, out_41);
  and and_24 (and_24_out, not_6_out, not_7_out, not_8_out, not_9_out, and_23_out);
  BitSelector #(.width(4)) bitselector_19 (.in(bitselector_17_out), .out(out_41), .sel(2'b01));
  not not_9 (not_9_out, out_42);
  and and_25 (and_25_out, not_6_out, not_7_out, not_8_out, out_42, and_23_out);
  BitSelector bitselector_20 ();  // open: in, out, sel
  BitSelector #(.width(4)) bitselector_21 (.in(bitselector_17_out), .out(out_42), .sel(2'b00));
  and and_26 (and_26_out, not_6_out, not_7_out, out_41, not_9_out, and_23_out);
  and and_27 (and_27_out, not_6_out, not_7_out, out_41, out_42, and_23_out);
  Multiplexer #(.select(5), .width(32), .enable("false")) multiplexer_5 (
    .in0(register_2_q), .in1(register_3_q), .in2(register_4_q), .in3(register_5_q), .in4(register_6_q),
    .in5(register_7_q), .in6(register_8_q), .in7(register_9_q), .in8(register_10_q), .in9(register_11_q),
    .in10(register_12_q), .in11(register_13_q), .in12(register_14_q), .in13(register_15_q),
    .in14(register_16_q), .out(multiplexer_5_out), .sel(out_23));  // open: in15, in16, in17, in18, in19, in20, in21, in22, in23, in24, in25, in26, in27, in28, in29, in30, in31
  Multiplexer #(.select(5), .width(32), .enable("false")) multiplexer_6 (
    .in0(register_2_q), .in1(register_3_q), .in2(register_4_q), .in3(register_5_q), .in4(register_6_q),
    .in5(register_7_q), .in6(register_8_q), .in7(register_9_q), .in8(register_10_q), .in9(register_11_q),
    .in10(register_12_q), .in11(register_13_q), .in12(register_14_q), .in13(register_15_q),
    .in14(register_16_q), .out(multiplexer_6_out), .sel(RD2));  // open: in15, in16, in17, in18, in19, in20, in21, in22, in23, in24, in25, in26, in27, in28, in29, in30, in31
  and and_28 (and_28_out, not_6_out, out_40, out_41, not_9_out, and_23_out);
  and and_29 (and_29_out, out_39, not_7_out, not_8_out, not_9_out, and_23_out);
  and and_30 (JRA, not_5_out, not_1_out, out_36, not_3_out, not_4_out);
  not not_10 (not_10_out, and_29_out);
  Multiplexer #(.width(32), .enable("false")) multiplexer_7 (
    .in0(multiplexer_5_out), .in1(adder_1_out), .out(multiplexer_7_out), .sel(savepc));
  Joystick joystick_1 (.x(out_18), .y(out_20));
  Multiplexer #(.width(32), .enable("false")) multiplexer_8 (
    .in0(multiplexer_6_out), .in1(bit_extender_3_out), .out(multiplexer_8_out), .sel(ALU_SRC));
  Bit_Extender #(.in_width(32), .out_width(5)) bit_extender_4 (.in(multiplexer_8_out), .out(bit_extender_4_out));
  and and_31 (and_31_out, and_23_out, not_10_out);
  or or_1 (MTRRTM, and_4_out, lui_out);
  assign and_32_out = multiplexer_7_out & multiplexer_8_out;  // AND_Gate and_32, 32 bits wide
  Adder #(.width(32)) adder_2 (
    .a(multiplexer_7_out), .b(multiplexer_8_out), .out(adder_2_out), .cin(1'b0));  // open: cout
  Subtractor #(.width(32)) subtractor_1 (
    .a(multiplexer_7_out), .b(multiplexer_8_out), .out(subtractor_1_out), .bin(1'b0));  // open: bout
  Multiplier #(.width(32)) multiplier_1 (
    .a(multiplexer_7_out), .b(multiplexer_8_out), .out(multiplier_1_out), .cin(undriven));  // open: cout
  Shifter #(.width(32), .shift("lr")) shifter_1 (
    .in(multiplexer_7_out), .\dist (bit_extender_4_out), .out(shifter_1_out));
  Divider #(.width(32)) divider_1 (
    .a(multiplexer_7_out), .b(multiplexer_8_out), .out(divider_1_out));  // open: upper, rem
  assign or_2_out = multiplexer_7_out | multiplexer_8_out;  // OR_Gate or_2, 32 bits wide
  or or_3 (BRAEN, and_5_out, BRE_BRNE);
  or or_4 (out_30, and_23_out, addi_out, savepc);
  or or_5 (ALU_SRC, addi_out, savepc);
  or or_6 (LD, and_1_out, and_3_out);
  or or_7 (out_28, and_2_out, and_3_out);
  or or_8 (out_33[2], and_29_out, IN_out);
  or or_9 (Bra, BRE_BRNE, and_5_out);
  or or_10 (out_47, IN_out, and_23_out, and_3_out, and_4_out, and_1_out, addi_out, lui_out, savepc);
  or or_11 (WRE_2, swi_out, and_2_out);
  or or_12 (out_33[0], and_31_out, addi_out, lui_out, IN_out, savepc);
  or or_13 (out_24[1], and_29_out, and_5_out, and_25_out, and_28_out, and_27_out, BRE_BRNE, and_29_out);
  or or_14 (out_24[0], and_24_out, and_28_out, addi_out, addi_out, savepc);
  or or_15 (out_24[2], and_27_out, and_27_out, shr_out);
  BitFinder #(.width(32)) bitfinder_1 (.in(multiplexer_9_out), .found(bitfinder_1_found));  // open: index
  BitSelector #(.width(32)) bitselector_22 (.in(multiplexer_9_out), .out(bitselector_22_out), .sel({5{1'b1}}));
  Bit_Extender #(.in_width(32), .out_width(24)) bit_extender_5 (.in(multiplexer_6_out), .out(bit_extender_5_out));
  Bit_Extender #(.in_width(32), .out_width(24)) bit_extender_6 (.in(bit_extender_3_out), .out(bit_extender_6_out));
  and and_33 (and_33_out, Bra, multiplexer_10_out);
  not not_11 (not_11_out, bitfinder_1_found);
  Multiplexer #(.select(3), .width(32), .enable("false")) multiplexer_9 (
    .in0(and_32_out), .in1(adder_2_out), .in2(subtractor_1_out), .in3(multiplier_1_out), .in4(shifter_1_out),
    .in5(divider_1_out), .in6(or_2_out), .out(multiplexer_9_out), .sel(out_24));  // open: in7
  assign bit_extender_7_out = {{31{1'b0}}, bitselector_22_out};  // Bit_Extender bit_extender_7
  Multiplexer multiplexer_10 (
    .in0(not_11_out), .in1(bitfinder_1_found), .out(multiplexer_10_out), .sel(BRE_BRNE), .en(BRAEN));
  Multiplexer #(.width(24), .enable("false")) multiplexer_11 (
    .in0(bit_extender_6_out), .in1(bit_extender_5_out), .out(multiplexer_11_out), .sel(out_28));
  Shifter #(.width(32)) shifter_2 (.in(bit_extender_3_out), .\dist (5'b10000), .out(shifter_2_out));
  Clock clock_3 (.out(clock_3_out));
  Multiplexer #(.select(3), .width(32), .enable("false")) multiplexer_12 (
    .in0(ram_1_data), .in1(multiplexer_9_out), .in2(multiplexer_6_out), .in3(shifter_2_out),
    .in4(bit_extender_7_out), .in5(bit_extender_8_out), .out(multiplexer_12_out),
    .sel({out_33[2], MTRRTM, out_33[0]}));  // open: in6, in7
  RAM #(.addrWidth(24), .dataWidth(32), .bus("separate")) ram_1 (
    .addr(multiplexer_11_out), .din(multiplexer_7_out), .data(ram_1_data), .str(WRE_2), .clk(clock_3_out),
    .ld(LD));  // open: sel, clr
  assign bit_extender_8_out = {{24{1'b0}}, multiplexer_13_out};  // Bit_Extender bit_extender_8
  TTY tty_1 (.data(in_11), .clk(in_12), .we(in_13), .clr(in_14));
  Decoder #(.select(4), .enable("false")) decoder_2 (
    .out0(decoder_2_out0), .out1(decoder_2_out1), .out2(decoder_2_out2), .out3(decoder_2_out3),
    .out4(decoder_2_out4), .out5(decoder_2_out5), .out6(decoder_2_out6), .out7(decoder_2_out7),
    .sel(bit_extender_9_out));  // open: out8, out9, out10, out11, out12, out13, out14, out15
  Bit_Extender #(.in_width(24), .out_width(4)) bit_extender_9 (.in(multiplexer_11_out), .out(bit_extender_9_out));
  Bit_Extender #(.in_width(32), .out_width(8)) bit_extender_10 (.in(multiplexer_7_out), .out(bit_extender_10_out));
  and and_34 (and_34_out, out_60, decoder_2_out0);
  and and_35 (and_35_out, out_60, decoder_2_out1);
  // AND_Gate and_36 has open pins: in0=out_60, in1=decoder_2_out2, out=open
  and and_37 (and_37_out, out_60, decoder_2_out3);
  and and_38 (and_38_out, out_60, decoder_2_out4);
  and and_39 (and_39_out, out_60, decoder_2_out5);
  and and_40 (and_40_out, out_60, decoder_2_out6);
  and and_41 (and_41_out, out_60, decoder_2_out7);
  Clock clock_4 (.out(clock_4_out));
  Register register_17 (.D(bit_extender_10_out), .en(and_34_out), .Q(register_17_q), .clk(clock_4_out), .clr(1'b0));
  Register register_18 (.D(bit_extender_10_out), .en(and_35_out), .Q(register_18_q), .clk(clock_4_out), .clr(1'b0));
  Register register_19 (.D(buffer_1_out), .en(1'b1), .Q(register_19_q), .clk(clock_4_out), .clr(1'b0));
  Register register_20 (.D(bit_extender_10_out), .en(and_37_out), .Q(register_20_q), .clk(clock_4_out), .clr(1'b0));
  Register register_21 (.D(bit_extender_10_out), .en(and_38_out), .Q(register_21_q), .clk(clock_4_out), .clr(1'b0));
  Register register_22 (.D(bit_extender_10_out), .en(and_39_out), .Q(register_22_q), .clk(clock_4_out), .clr(1'b0));
  Register register_23 (.D(bit_extender_10_out), .en(and_40_out), .Q(register_23_q), .clk(clock_4_out), .clr(1'b0));
  Register register_24 (.D(bit_extender_10_out), .en(and_41_out), .Q(register_24_q), .clk(clock_4_out), .clr(1'b0));
  Multiplexer #(.select(4), .width(8), .enable("false")) multiplexer_13 (
    .in0(register_17_q), .in1(register_18_q), .in2(register_19_q), .in3(register_20_q), .in4(register_24_q),
    .in5(register_23_q), .in6(register_22_q), .in7(register_21_q), .out(multiplexer_13_out),
    .sel(bit_extender_9_out));  // open: in8, in9, in10, in11, in12, in13, in14, in15
  assign in_1 = register_18_q[0] ? register_17_q[0] : 1'bz;  // Controlled_Buffer controlled_buffer_1
  assign in_3 = register_18_q[1] ? register_17_q[1] : 1'bz;  // Controlled_Buffer controlled_buffer_2
  assign in_4 = register_18_q[2] ? register_17_q[2] : 1'bz;  // Controlled_Buffer controlled_buffer_3
  assign in_5 = register_18_q[3] ? register_17_q[3] : 1'bz;  // Controlled_Buffer controlled_buffer_4
  assign in_6 = register_18_q[4] ? register_17_q[4] : 1'bz;  // Controlled_Buffer controlled_buffer_5
  assign in_7 = register_18_q[5] ? register_17_q[5] : 1'bz;  // Controlled_Buffer controlled_buffer_6
  assign in_8 = register_18_q[6] ? register_17_q[6] : 1'bz;  // Controlled_Buffer controlled_buffer_7
  assign in_9 = register_18_q[7] ? register_17_q[7] : 1'bz;  // Controlled_Buffer controlled_buffer_8
  buf buffer_1 (buffer_1_out[0], in_1);
  buf buffer_2 (buffer_1_out[1], in_3);
  buf buffer_3 (buffer_1_out[2], in_4);
  buf buffer_4 (buffer_1_out[3], in_5);
  buf buffer_5 (buffer_1_out[4], in_6);
  buf buffer_6 (buffer_1_out[5], in_7);
  buf buffer_7 (buffer_1_out[6], in_8);
  buf buffer_8 (buffer_1_out[7], in_9);
  LED led_1 (.in(in_1));
  TTY tty_2 ();  // open: data, clk, we, clr

  assign ALUSRC = ALU_SRC;
  assign BRA_2 = Bra;
  assign BRE_NE = BRE_BRNE;
  assign jmp = J;
  assign JRA_2 = JRA;
  assign LoadOutput = LD;
  assign out_21 = BRAEN;
  assign out_33[1] = MTRRTM;
  assign out_46 = out_30;
  assign out_51 = out_28;
  assign out_52 = out_33[2];
  assign out_54 = out_33[0];
  assign out_56 = out_24[2];
  assign out_57 = out_24[1];
  assign out_58 = out_24[0];
  assign SpecialRegEnable = out_60;
  assign WRE = out_47;
  assign WRE_3 = WRE_2;

  // Notes on the sheet:
  //   Bra
  //   lwi
  //   Interrupt mekanizması eklenecek GIE ekle interrupt çalıştığında ilk komut bu olacak
  //   contents of rom_1 (hex, n*v repeats v):
  //   6000000a 9*0 1800007b c0520000 1800009b c0920000 440000 c2520000 a400002 180000ff c0520000 30400001
  //   30400000 18000000 c0520000 30400000 18000001 c0520000 30400000 60000015
  //   lw
  //   result reg
  //   17:13
  //   sw
  //   5,6 işlemlerde değişiyor..
  //   27:23
  //   mov
  //   RegDst Sel
  //   22:18
  //   RD1
  //   beq
  //   bneq
  //   J
  //   R-Type
  //   add
  //   sub
  //   or
  //   and
  //   mul
  //   savepc
  //   slt
  //   JRA
  //   RegDstSel
  //   RFWE
  //   MemorySrc
  //   ALUOP
  //   SpecialRegFileEnable
  //   for reg = reg
  //   Direk registerdan
  //   Branch Enable
  //   MUX ekle Adrese
  //   Memory Adres Source
  //   PORT registerlarını adreesini buradan alacağız
  //   DataSourceToRegFile
  //   PORTA
  //   TRISA
  //   PINA
endmodule
