// Logisim project MyProcessorController.circ as structural Verilog: 1 circuit, main circuit main
module main (
  input  in_1,
  input  in_2,
  input  in_3,
  input  in_4,
  input  in_5,
  input  in_6,
  input  in_7,
  input  in_8,
  input  in_9,
  output BRAEN,
  output BRE_NE,
  output JRA,
  output out_13,
  output out_14,
  output ALUSRC,
  output WRE,
  output LD,
  output out_18,
  output out_19,
  output MTRRTM,
  output out_21,
  output J,
  output out_23,
  output out_24,
  output out_25
);

  wire and_1_out, and_2_out, and_3_out, and_4_out, and_5_out, and_8_out, and_9_out, and_10_out, and_11_out,
       and_12_out, and_13_out, and_14_out, and_16_out, lui_out, not_1_out, not_2_out, not_3_out, not_4_out,
       not_5_out, not_6_out, not_7_out, not_8_out, not_9_out, not_10_out, swi_out;

  and and_1 (and_1_out, not_5_out, not_2_out, not_1_out, in_8, not_3_out);
  and swi (swi_out, not_5_out, not_2_out, not_1_out, not_4_out, in_9);
  and lui (lui_out, not_5_out, not_2_out, in_7, in_8, in_9);
  and addi (ALUSRC, not_5_out, not_2_out, not_1_out, in_8, in_9);
  not not_1 (not_1_out, in_7);
  not not_2 (not_2_out, in_6);
  and and_2 (and_2_out, in_5, not_2_out, not_1_out, not_4_out, not_3_out);
  not not_3 (not_3_out, in_9);
  not not_4 (not_4_out, in_8);
  not not_5 (not_5_out, in_5);
  and and_3 (and_3_out, not_5_out, in_6, not_1_out, not_4_out, not_3_out);
  and and_4 (and_4_out, in_5, in_6, not_1_out, not_4_out, not_3_out);
  and and_5 (and_5_out, in_5, not_2_out, in_7, not_4_out, not_3_out);
  and and_6 (BRE_NE, in_5, in_6, in_7, not_4_out, not_3_out);
  and and_7 (J, not_5_out, in_6, in_7, not_4_out, not_3_out);
  and and_8 (and_8_out, not_5_out, not_2_out, not_1_out, not_4_out, not_3_out);
  not not_6 (not_6_out, in_2);
  not not_7 (not_7_out, in_1);
  and and_9 (and_9_out, not_7_out, not_6_out, not_8_out, not_9_out, and_8_out);
  not not_8 (not_8_out, in_3);
  not not_9 (not_9_out, in_4);
  and and_10 (and_10_out, not_7_out, not_6_out, not_8_out, in_4, and_8_out);
  and and_11 (and_11_out, not_7_out, not_6_out, in_3, not_9_out, and_8_out);
  and and_12 (and_12_out, not_7_out, in_2, in_3, not_9_out, and_8_out);
  and and_13 (and_13_out, not_7_out, not_6_out, in_3, in_4, and_8_out);
  and and_14 (and_14_out, in_1, not_6_out, not_8_out, not_9_out, and_8_out);
  not not_10 (not_10_out, and_14_out);
  and and_15 (JRA, not_5_out, not_2_out, in_7, not_4_out, not_3_out);
  and and_16 (and_16_out, and_8_out, not_10_out);
  or or_1 (MTRRTM, and_4_out, lui_out);
  or or_2 (BRAEN, and_5_out, BRE_NE);
  or or_3 (out_13, and_8_out, ALUSRC);
  or or_4 (LD, and_1_out, and_3_out);
  or or_5 (out_18, and_2_out, and_3_out);
  buf or_6 (out_19, and_14_out);  // OR_Gate
  or or_7 (out_14, and_8_out, and_3_out, and_4_out, and_1_out, ALUSRC, lui_out);
  or or_8 (WRE, swi_out, and_2_out);
  or or_9 (out_21, and_16_out, ALUSRC, lui_out);
  or or_10 (out_24, and_14_out, and_5_out, and_10_out, and_10_out, and_13_out, BRE_NE, and_14_out);
  or or_11 (out_23, and_12_out, and_13_out);
  or or_12 (out_25, and_9_out, and_12_out, ALUSRC, ALUSRC);

  // Notes on the sheet:
  //   lwi
  //   lw
  //   sw
  //   mov
  //   beq
  //   bneq
  //   J
  //   R-Type
  //   add
  //   sub
  //   or
  //   and
  //   mul
  //   slt
  //   JRA
  //   RegDstSel
  //   RFWE
  //   MemorySrc
  //   ALUOP
endmodule
