// Logisim project RegFile.circ as structural Verilog: 1 circuit, main circuit main
module main (
);

  wire decoder_1_out0, decoder_1_out1, decoder_1_out2, decoder_1_out3, decoder_1_out4, undriven_2;
  wire [4:0] undriven;
  wire [31:0] multiplexer_1_out, register_1_q, register_2_q, register_3_q, register_4_q, register_5_q,
       register_6_q;

  Decoder #(.select(5)) decoder_1 (
    .out0(decoder_1_out0), .out1(decoder_1_out1), .out2(decoder_1_out2), .out3(decoder_1_out3),
    .out4(decoder_1_out4), .sel(undriven), .en(undriven_2));  // open: out5, out6, out7, out8, out9, out10, out11, out12, out13, out14, out15, out16, out17, out18, out19, out20, out21, out22, out23, out24, out25, out26, out27, out28, out29, out30, out31
  Decoder #(.select(5)) decoder_2 ();  // open: out0, out1, out2, out3, out4, out5, out6, out7, out8, out9, out10, out11, out12, out13, out14, out15, out16, out17, out18, out19, out20, out21, out22, out23, out24, out25, out26, out27, out28, out29, out30, out31, sel, en
  Decoder #(.select(5)) decoder_3 ();  // open: out0, out1, out2, out3, out4, out5, out6, out7, out8, out9, out10, out11, out12, out13, out14, out15, out16, out17, out18, out19, out20, out21, out22, out23, out24, out25, out26, out27, out28, out29, out30, out31, sel, en
  Register #(.width(32)) register_1 (.en(decoder_1_out0), .Q(register_1_q));  // open: D, clk, clr
  Register #(.width(32)) register_2 (.en(decoder_1_out1), .Q(register_2_q));  // open: D, clk, clr
  Register #(.width(32)) register_3 (.en(decoder_1_out2), .Q(register_3_q));  // open: D, clk, clr
  Register #(.width(32)) register_4 (.en(decoder_1_out3), .Q(register_4_q));  // open: D, clk, clr
  Register #(.width(32)) register_5 (.en(decoder_1_out4), .Q(register_5_q));  // open: D, clk, clr
  Register #(.width(32)) register_6 (.Q(register_6_q));  // open: D, en, clk, clr
  Register #(.width(32)) register_7 ();  // open: D, en, Q, clk, clr
  Register #(.width(32)) register_8 ();  // open: D, en, Q, clk, clr
  Register #(.width(32)) register_9 ();  // open: D, en, Q, clk, clr
  Multiplexer #(.select(5), .width(32)) multiplexer_1 (
    .in0(register_1_q), .in1(register_2_q), .in2(register_3_q), .in3(register_4_q), .in4(register_5_q),
    .in5(register_6_q), .out(multiplexer_1_out), .sel(undriven), .en(undriven_2));  // open: in6, in7, in8, in9, in10, in11, in12, in13, in14, in15, in16, in17, in18, in19, in20, in21, in22, in23, in24, in25, in26, in27, in28, in29, in30, in31
endmodule
